// Logisim project s-mips.circ as structural Verilog
module S_MIPS_Board (
  input  DESHABILITAR_DISPATCHER,
  output halt
);

  wire button_1_out, CLK, CS, d_ff_1_q, LCLR, LoadRAM, LoadRAMOn, LW, R_R_W, R_W, ram_dispatcher_1_finished,
       RCS, Reset_out, RST, TTY_EN;
  wire [2:0] KDB;
  wire [3:0] LMask, Mask, ram_1_read_time, ram_1_write_time, RMask;
  wire [6:0] KDB_DATA, TTY_DATA;
  wire [15:0] Addr, LAddr, RAddr;
  wire [31:0] I0, I1, I2, I3, LData, ram_1_data_out_0, ram_1_data_out_1, ram_1_data_out_2, ram_1_data_out_3,
       RI0, RI1, RI2, RI3;

  TTY #(.rows(25), .cols(80)) tty_1 (.data(TTY_DATA), .clk(CLK), .we(TTY_EN), .clr(RST));
  not not_1 (LoadRAMOn, ram_dispatcher_1_finished);
  RAM_Dispatcher ram_dispatcher_1 (
    .WriteTime(ram_1_write_time), .Clock(CLK), .Data(LData), .Address(LAddr), .Mask(LMask),
    .Finished(ram_dispatcher_1_finished), .Write(LW), .CLR(LCLR));
  Keyboard #(.buflen(64)) keyboard_1 (.clk(CLK), .re(KDB[0]), .avail(KDB[2]), .data(KDB_DATA));  // open: clr
  RAM ram_1 (
    .Address(RAddr), .Data_Out_0(ram_1_data_out_0), .Data_Out_1(ram_1_data_out_1),
    .Data_Out_2(ram_1_data_out_2), .Data_Out_3(ram_1_data_out_3), .Data_In_0(RI0), .Data_In_1(RI1),
    .Data_In_2(RI2), .Data_In_3(RI3), .Mask(RMask), .nRead_Write(R_R_W), .Chip_Select(RCS),
    .Read_Time(ram_1_read_time), .Reset(button_1_out), .Write_Time(ram_1_write_time));
  Button button_1 (.out(button_1_out));
  D_Flip_Flop d_ff_1 (.clk(CLK), .D(1'b1), .Q(d_ff_1_q), .reset(Reset_out));  // open: Qn, preset, en
  Button Reset (.out(Reset_out));
  S_MIPS s_mips_1 (
    .Kbd_Enable(KDB[0]), .Address(Addr), .Kbd_Clear(KDB[1]), .Kbd_Available(KDB[2]), .RAM_In_0(I0),
    .Kbd_ASCII_Data(KDB_DATA), .RAM_In_1(I1), .TTY_Enable(TTY_EN), .RAM_In_2(I2), .RAM_In_3(I2),
    .TTY_ASCII_Data(TTY_DATA), .Reset(RST), .RAM_Out_0(ram_1_data_out_0), .Clock(CLK),
    .RAM_Out_1(ram_1_data_out_1), .Stop(halt), .RAM_Out_2(ram_1_data_out_2), .RAM_Out_3(ram_1_data_out_3),
    .Mask(Mask), .Read_Time(ram_1_read_time), .Write_Time(ram_1_write_time), .nRead_Write(R_W),
    .Chip_Select(CS));
  D_Flip_Flop d_ff_2 (.clk(CLK), .D(d_ff_1_q), .Qn(LCLR), .reset(Reset_out));  // open: Q, preset, en
  or or_1 (RST, LCLR, LoadRAM);
  Clock clock_1 (.out(CLK));
  Multiplexer #(.width(32), .enable("false")) multiplexer_1 (.in0(I0), .in1(LData), .out(RI0), .sel(LoadRAM));
  Multiplexer #(.width(32), .enable("false")) multiplexer_2 (.in0(I1), .in1(LData), .out(RI1), .sel(LoadRAM));
  Multiplexer #(.width(32), .enable("false")) multiplexer_3 (.in0(I2), .in1(LData), .out(RI2), .sel(LoadRAM));
  Multiplexer #(.width(32), .enable("false")) multiplexer_4 (.in0(I3), .in1(LData), .out(RI3), .sel(LoadRAM));
  and and_1 (LoadRAM, ~DESHABILITAR_DISPATCHER, LoadRAMOn);  // AND_Gate
  Multiplexer #(.width(16), .enable("false")) multiplexer_5 (.in0(Addr), .in1(LAddr), .out(RAddr), .sel(LoadRAM));
  Multiplexer #(.width(4), .enable("false")) multiplexer_6 (.in0(Mask), .in1(LMask), .out(RMask), .sel(LoadRAM));
  Multiplexer #(.enable("false")) multiplexer_7 (.in0(CS), .in1(LW), .out(RCS), .sel(LoadRAM));
  Multiplexer #(.enable("false")) multiplexer_8 (.in0(R_W), .in1(LW), .out(R_R_W), .sel(LoadRAM));

  // Notes on the sheet:
  //   NO MODIFICAR
  //   Keyboard
endmodule

module RAM (
  input  [15:0] Address,
  input  [31:0] Data_In_0,
  input  [31:0] Data_In_1,
  input  [31:0] Data_In_2,
  input  [31:0] Data_In_3,
  input  [3:0] Mask,
  input  nRead_Write,
  input  Chip_Select,
  input  Reset,
  output [31:0] Data_Out_0,
  output [31:0] Data_Out_1,
  output [31:0] Data_Out_2,
  output [31:0] Data_Out_3,
  output [3:0] Read_Time,
  output [3:0] Write_Time
);

  wire and_2_out, and_3_out, and_4_out, and_5_out, and_6_out, and_7_out, and_8_out, and_9_out, Changed, CLK,
       comparator_2_eq, comparator_3_eq, comparator_4_eq, comparator_5_eq, comparator_6_eq, Count,
       demultiplexer_3_out0, Idle, Idle_q, Load, Load0, Load1, nand_1_out, or_1_out, or_2_out, or_3_out,
       or_4_out, or_5_out, or_6_out, or_7_out, or_8_out, or_9_out, or_10_out, Proc_q, Update_Mem, Zero_Time;
  wire [3:0] counter_1_q, multiplexer_1_out, subtractor_1_out;
  wire [31:0] register_1_q, register_2_q, register_3_q, register_4_q, register_5_q;

  // Probe on 4'b0011
  // Probe on 4'b0010
  Multiplexer #(.width(4), .enable("false")) multiplexer_1 (
    .in0(4'b0011), .in1(4'b0010), .out(multiplexer_1_out), .sel(nRead_Write));
  or or_1 (or_1_out, Idle, Update_Mem);
  or or_2 (or_2_out, ~Chip_Select, Reset);  // OR_Gate
  Subtractor #(.width(4)) subtractor_1 (.a(multiplexer_1_out), .b(4'b0010), .out(subtractor_1_out));  // open: bin, bout
  D_Flip_Flop u_Idle (.clk(CLK), .D(or_1_out), .Q(Idle_q), .preset(or_2_out));  // open: Qn, en, reset
  Demultiplexer #(.enable("false")) demultiplexer_1 (.out0(Idle), .out1(Load0), .in(Idle_q), .sel(Changed));
  // Probe on counter_1_q
  Counter #(.width(4), .max('hf)) counter_1 (
    .load(Load), .D(subtractor_1_out), .count(Count), .Q(counter_1_q), .clk(CLK), .clr(or_3_out));  // open: carry
  or or_3 (or_3_out, ~Chip_Select, Reset);  // OR_Gate
  Comparator #(.width(4), .mode("unsigned")) comparator_1 (
    .a(4'b0000), .b(counter_1_q), .eq(Zero_Time));  // open: gt, lt
  or or_4 (or_4_out, Count, Load0, Load1);
  Register #(.width(32)) register_1 (.D(Data_In_0), .en(Chip_Select), .Q(register_1_q), .clk(CLK), .clr(or_5_out));
  or or_5 (or_5_out, ~Chip_Select, Reset);  // OR_Gate
  Register #(.width(32)) register_2 (.D(Data_In_1), .en(Chip_Select), .Q(register_2_q), .clk(CLK), .clr(or_6_out));
  or or_6 (or_6_out, ~Chip_Select, Reset);  // OR_Gate
  Register #(.width(32)) register_3 (.D(Data_In_2), .en(Chip_Select), .Q(register_3_q), .clk(CLK), .clr(or_7_out));
  or or_7 (or_7_out, ~Chip_Select, Reset);  // OR_Gate
  Register #(.width(32)) register_4 (.D(Data_In_3), .en(Chip_Select), .Q(register_4_q), .clk(CLK), .clr(or_8_out));
  or or_8 (or_8_out, ~Chip_Select, Reset);  // OR_Gate
  Register #(.width(32)) register_5 (
    .D({{11{1'b1}}, nRead_Write, Mask, Address}), .en(Chip_Select), .Q(register_5_q), .clk(CLK),
    .clr(or_9_out));
  or or_9 (or_9_out, ~Chip_Select, Reset);  // OR_Gate
  D_Flip_Flop Proc (.clk(CLK), .D(or_4_out), .Q(Proc_q), .reset(or_10_out));  // open: Qn, preset, en
  or or_10 (or_10_out, ~Chip_Select, Reset);  // OR_Gate
  Demultiplexer #(.enable("false")) demultiplexer_2 (
    .out0(Count), .out1(Update_Mem), .in(demultiplexer_3_out0), .sel(Zero_Time));
  Demultiplexer #(.enable("false")) demultiplexer_3 (
    .out0(demultiplexer_3_out0), .out1(Load1), .in(Proc_q), .sel(Changed));
  Clock clock_1 (.out(CLK));
  Comparator #(.width(32)) comparator_2 (.a(register_1_q), .b(Data_In_0), .eq(comparator_2_eq));  // open: gt, lt
  Comparator #(.width(32)) comparator_3 (.a(register_2_q), .b(Data_In_1), .eq(comparator_3_eq));  // open: gt, lt
  Comparator #(.width(32)) comparator_4 (.a(register_3_q), .b(Data_In_2), .eq(comparator_4_eq));  // open: gt, lt
  Comparator #(.width(32)) comparator_5 (.a(register_4_q), .b(Data_In_3), .eq(comparator_5_eq));  // open: gt, lt
  Comparator #(.width(32)) comparator_6 (
    .a(register_5_q), .b({{11{1'b1}}, nRead_Write, Mask, Address}), .eq(comparator_6_eq));  // open: gt, lt
  nand nand_1 (nand_1_out, comparator_6_eq, comparator_2_eq, comparator_3_eq, comparator_4_eq, comparator_5_eq);
  and and_1 (Changed, nand_1_out, Chip_Select);
  or or_11 (Load, Count, Load1, Load0);
  and and_2 (and_2_out, Mask[0], Update_Mem, nRead_Write);
  and and_3 (and_3_out, Mask[1], Update_Mem, nRead_Write);
  and and_4 (and_4_out, Mask[2], Update_Mem, nRead_Write);
  and and_5 (and_5_out, Mask[3], Update_Mem, nRead_Write);
  RAM_part #(.addrWidth(16), .dataWidth(32), .bus("separate")) ram_1 (
    .addr(Address), .din(Data_In_0), .data(Data_Out_0), .str(and_2_out), .sel(Chip_Select), .clk(CLK),
    .ld(and_6_out), .clr(Reset));
  and and_6 (and_6_out, ~nRead_Write, Idle);  // AND_Gate
  RAM_part #(.addrWidth(16), .dataWidth(32), .bus("separate")) ram_2 (
    .addr(Address), .din(Data_In_1), .data(Data_Out_1), .str(and_3_out), .sel(Chip_Select), .clk(CLK),
    .ld(and_7_out), .clr(Reset));
  and and_7 (and_7_out, ~nRead_Write, Idle);  // AND_Gate
  RAM_part #(.addrWidth(16), .dataWidth(32), .bus("separate")) ram_3 (
    .addr(Address), .din(Data_In_2), .data(Data_Out_2), .str(and_4_out), .sel(Chip_Select), .clk(CLK),
    .ld(and_8_out), .clr(Reset));
  and and_8 (and_8_out, ~nRead_Write, Idle);  // AND_Gate
  RAM_part #(.addrWidth(16), .dataWidth(32), .bus("separate")) ram_4 (
    .addr(Address), .din(Data_In_3), .data(Data_Out_3), .str(and_5_out), .sel(Chip_Select), .clk(CLK),
    .ld(and_9_out), .clr(Reset));
  and and_9 (and_9_out, ~nRead_Write, Idle);  // AND_Gate

  assign Read_Time = 4'b0011;
  assign Write_Time = 4'b0010;

  // Other names for the same wires on the sheet: M0 = Mask[0]; M1 = Mask[1]; M2 = Mask[2]; M3 = Mask[3];
  //   RW = nRead_Write; CLR = Reset; CS = Chip_Select; Load2 = Count

  // Notes on the sheet:
  //   NO MODIFICAR
  //   excepto quizás los valores RT y WT
  //   BANK0
  //   BANK1
  //   BANK2
  //   BANK3
endmodule

module S_MIPS (
  input  Kbd_Available,
  input  [6:0] Kbd_ASCII_Data,
  input  [31:0] RAM_Out_0,
  input  [31:0] RAM_Out_1,
  input  Reset,
  input  [31:0] RAM_Out_2,
  input  Clock,
  input  [31:0] RAM_Out_3,
  input  [3:0] Read_Time,
  input  [3:0] Write_Time,
  output Kbd_Enable,
  output [15:0] Address,
  output Kbd_Clear,
  output TTY_Enable,
  output [6:0] TTY_ASCII_Data,
  output Stop,
  output [31:0] RAM_In_0,
  output [31:0] RAM_In_1,
  output [31:0] RAM_In_2,
  output [31:0] RAM_In_3,
  output [3:0] Mask,
  output nRead_Write,
  output Chip_Select
);


  // Other names for the same wires on the sheet: CLK = Clock; CLR = Reset; CS = Chip_Select;
  //   KBD_AVAIL = Kbd_Available; KBD_CLR = Kbd_Clear; KBD_DATA[6:0] = Kbd_ASCII_Data; RAM_A[15:0] = Address;
  //   RAM_INPUT_0[31:0] = RAM_In_0; RAM_INPUT_1[31:0] = RAM_In_1; RAM_INPUT_2[31:0] = RAM_In_2;
  //   RAM_INPUT_3[31:0] = RAM_In_3; RAM_MASK[3:0] = Mask; RAM_OUTPUT_0[31:0] = RAM_Out_0;
  //   RAM_OUTPUT_1[31:0] = RAM_Out_1; RAM_OUTPUT_2[31:0] = RAM_Out_2; RAM_OUTPUT_3[31:0] = RAM_Out_3;
  //   RW = nRead_Write; TTY_DATA[6:0] = TTY_ASCII_Data

  // Notes on the sheet:
  //   RAM ADDRESS
  //   DATA FROM RAM
  //   DATA TO RAM
  //   DATA WRITE MASK
  //   RAM TIMING
  //   RAM CONTROL
  //   KEYBOARD
  //   TTY
  //   SEQUENCING
endmodule

module RAM_Dispatcher (
  input  [3:0] WriteTime,
  input  Clock,
  input  CLR,
  output [31:0] Data,
  output [15:0] Address,
  output [3:0] Mask,
  output Finished,
  output Write
);

  wire demultiplexer_2_out1, demultiplexer_3_out1, End, IDLE_q, IncAddr, Load, or_1_out, or_2_out, While_q,
       WriteEnd;
  wire [3:0] counter_1_q;
  wire [31:0] CurrentAddress_q;

  Counter #(.width(32), .max('hffffffff)) CurrentAddress (
    .count(IncAddr), .Q({CurrentAddress_q[31:18], Address, CurrentAddress_q[1:0]}), .clk(Clock), .clr(CLR));  // open: load, D, carry
  or or_1 (or_1_out, IncAddr, demultiplexer_3_out1, Finished);
  D_Flip_Flop IDLE (.clk(Clock), .D(or_1_out), .Q(IDLE_q), .preset(CLR));  // open: Qn, en, reset
  Demultiplexer #(.enable("false")) demultiplexer_1 (.out0(Load), .out1(Finished), .in(IDLE_q), .sel(End));
  D_Flip_Flop While (.clk(Clock), .D(or_2_out), .Q(While_q), .reset(CLR));  // open: Qn, preset, en
  or or_2 (or_2_out, Write, Load);
  RAM_part #(.addrWidth(18), .dataWidth(32)) ram_1 (
    .addr({Address, CurrentAddress_q[1:0]}), .data(Data), .clk(Clock));  // open: sel, ld, clr
  Demultiplexer #(.enable("false")) demultiplexer_2 (
    .out0(Write), .out1(demultiplexer_2_out1), .in(While_q), .sel(WriteEnd));
  Decoder #(.select(2)) decoder_1 (
    .out0(Mask[0]), .out1(Mask[1]), .out2(Mask[2]), .out3(Mask[3]), .sel(CurrentAddress_q[1:0]));  // open: en
  Demultiplexer #(.enable("false")) demultiplexer_3 (
    .out0(IncAddr), .out1(demultiplexer_3_out1), .in(demultiplexer_2_out1), .sel(End));
  Counter #(.width(4), .max('hf)) counter_1 (
    .load(Load), .D(WriteTime), .count(Write), .Q(counter_1_q), .clk(Clock));  // open: carry, clr
  Comparator #(.width(32)) comparator_1 (.a(Data), .b({32{1'b1}}), .eq(End));  // open: gt, lt
  Comparator #(.width(4)) comparator_2 (.a(4'b0000), .b(counter_1_q), .eq(WriteEnd));  // open: gt, lt

  // Other names for the same wires on the sheet: CLK = Clock; Count = Write; WT[3:0] = WriteTime
endmodule

module Branch_Control_Unit (
  input  [5:0] in_1,
  input  [4:0] in_2,
  input  [4:0] Input,
  input  [25:0] in_4,
  input  [15:0] in_5,
  input  [5:0] in_6,
  input  [4:0] in_7,
  input  [4:0] in_8
);

  wire add, \and , div, divu, I, IE, J, mult, mulu, nop, \nor , \or , P, R, slt, sltu, sub, \xor ;

  Comparator #(.width(6)) comparator_1 (.a(in_1), .b({6{1'b0}}), .eq(R));  // open: gt, lt
  Comparator #(.width(6)) comparator_2 (.a(in_1), .b(6'b001000), .eq(J));  // open: gt, lt
  Comparator #(.width(6)) comparator_3 (.a(in_1), .b(6'b011000), .eq(P));  // open: gt, lt
  Comparator #(.width(6)) comparator_4 (.a(in_1), .b(6'b000111), .eq(IE));  // open: gt, lt
  nor nor_1 (I, R, J, P, IE);
  Comparator #(.width(6)) comparator_5 (.a(in_6), .b({6{1'b0}}), .eq(nop));  // open: gt, lt
  Comparator #(.width(6)) comparator_6 (.a(in_6), .b(6'b100000), .eq(add));  // open: gt, lt
  Comparator #(.width(6)) comparator_7 (.a(in_6), .b(6'b101010), .eq(sub));  // open: gt, lt
  Comparator #(.width(6)) comparator_8 (.a(in_6), .b({6{1'b0}}), .eq(mult));  // open: gt, lt
  Comparator #(.width(6)) comparator_9 (.a(in_6), .b(6'b000001), .eq(mulu));  // open: gt, lt
  Comparator #(.width(6)) comparator_10 (.a(in_6), .b(6'b001000), .eq(div));  // open: gt, lt
  Comparator #(.width(6)) comparator_11 (.a(in_6), .b(6'b001001), .eq(divu));  // open: gt, lt
  Comparator #(.width(6)) comparator_12 (.a(in_6), .b(6'b010010), .eq(slt));  // open: gt, lt
  Comparator #(.width(6)) comparator_13 (.a(in_6), .b(6'b001000), .eq(\xor ));  // open: gt, lt
  Comparator #(.width(6)) comparator_14 (.a(in_6), .b(6'b010011), .eq(sltu));  // open: gt, lt
  Comparator #(.width(6)) comparator_15 (.a(in_6), .b(6'b000100), .eq(\and ));  // open: gt, lt
  Comparator #(.width(6)) comparator_16 (.a(in_6), .b(6'b000101), .eq(\or ));  // open: gt, lt
  Comparator #(.width(6)) comparator_17 (.a(in_6), .b(6'b001111), .eq(\nor ));  // open: gt, lt

  // Other names for the same wires on the sheet: Const[15:0] = in_5; Destino[25:0] = in_4; Func_Code[5:0] = in_6;
  //   Op_Code[5:0] = in_1; Rd[4:0] = Input; Rs[4:0] = in_2; Rt[4:0] = in_7; x[4:0] = in_8

  // Notes on the sheet:
  //   Tipo de instruccion
  //   Instrucciones de tipo R
endmodule

module Instruction_Decoder (
  input  [31:0] in_1,
  output [5:0] Op_Code,
  output [4:0] Rt,
  output [15:0] Constante,
  output [5:0] Func_Code,
  output [4:0] Rd,
  output [4:0] Rs,
  output [4:0] x,
  output [25:0] Destino_salto,
  output Output,
  output Output_2,
  output Output_3,
  output Output_4
);

  wire I;
  wire [5:0] Op_Code_t;

  Comparator #(.width(6)) comparator_1 (.a(Op_Code_t), .b({6{1'b0}}), .eq(Output));  // open: gt, lt
  Comparator #(.width(6)) comparator_2 (.a(Op_Code_t), .b(6'b001000), .eq(Output_2));  // open: gt, lt
  Comparator #(.width(6)) comparator_3 (.a(Op_Code_t), .b(6'b011000), .eq(Output_3));  // open: gt, lt
  Comparator #(.width(6)) comparator_4 (.a(Op_Code_t), .b(6'b000111), .eq(Output_4));  // open: gt, lt
  nor nor_1 (I, Output, Output_2, Output_3, Output_4);

  assign Constante = in_1[31:16];
  assign Destino_salto = in_1[31:6];
  assign Func_Code = in_1[31:26];
  assign Op_Code = in_1[5:0];
  assign Rd = in_1[20:16];
  assign Rs = in_1[10:6];
  assign Rt = in_1[15:11];
  assign x = in_1[20:16];

  // Other names for the same wires on the sheet: IE = Output_4; Input[31:0] = in_1; J = Output_2; P = Output_3;
  //   R = Output

  // Notes on the sheet:
  //   Instruction Decoder
  //   Tipo de instruccion
endmodule

module ALU_R (
  input  [5:0] in_1,
  input  in_2,
  input  [31:0] in_3,
  input  [31:0] in_4,
  input  [15:0] in_5,
  output Output,
  output [31:0] low,
  output [31:0] hi,
  output Output_2
);

  wire add, \and , con_signo, div, divu, mul, mulu, \nor , \or , slt, sltu, sub, \xor ;
  wire [3:0] priority_encoder_1_out, priority_encoder_2_out;
  wire [31:0] div___divu_hi, div__divu_hi, div__divu_lo, hi_t, low_t, mult___mulu_hi, mult___mulu_lo, result,
       s_add, s_and, s_nor, s_or, s_sub, s_xor, slt___sltu;

  Adder #(.width(32)) adder_1 (.a(in_3), .b(in_4), .out(s_add));  // open: cin, cout
  Subtractor #(.width(32)) subtractor_1 (.a(in_3), .b(in_4), .out(s_sub));  // open: bin, bout
  assign s_and = in_3 & in_4;  // AND_Gate and_1, 32 bits wide
  assign s_or = in_3 | in_4;  // OR_Gate or_1, 32 bits wide
  assign s_xor = in_3 ^ in_4;  // XOR_Gate xor_1, 32 bits wide
  assign s_nor = ~(in_3 | in_4);  // NOR_Gate nor_1, 32 bits wide
  and and_2 (add, ~in_1[0], ~in_1[1], ~in_1[2], ~in_1[3], ~in_1[4], in_1[5]);  // AND_Gate
  and and_3 (sub, ~in_1[0], in_1[1], ~in_1[2], ~in_1[3], ~in_1[4], in_1[5]);  // AND_Gate
  and and_4 (mul, ~in_1[0], ~in_1[1], ~in_1[2], in_1[3], in_1[4], ~in_1[5]);  // AND_Gate
  and and_5 (mulu, in_1[0], ~in_1[1], ~in_1[2], in_1[3], in_1[4], ~in_1[5]);  // AND_Gate
  Priority_Encoder #(.select(4)) priority_encoder_1 (
    .in0(add), .in1(sub), .in2(mul), .in3(mulu), .in4(div), .in5(divu), .in6(slt), .in7(sltu), .in8(\and ),
    .in9(\or ), .in10(\nor ), .in11(\xor ), .out(priority_encoder_1_out));  // open: in12, in13, in14, in15, gs, en_out, en_in
  Priority_Encoder #(.select(4)) priority_encoder_2 (
    .in0(add), .in1(sub), .in2(mul), .in3(mulu), .in4(div), .in5(divu), .in6(slt), .in7(sltu), .in8(\and ),
    .in9(\or ), .in10(\nor ), .in11(\xor ), .out(priority_encoder_2_out));  // open: in12, in13, in14, in15, gs, en_out, en_in
  div___divu div_divu_1 (.in_1(in_3), .in_2(in_4), .in_3(con_signo), .Hi(div__divu_lo), .Lo(div___divu_hi));
  slt___sltu slt_sltu_1 (.Rt(in_4), .Rs(in_3), .Output(slt___sltu), .in_1(con_signo));
  // Probe on priority_encoder_1_out
  // Probe on priority_encoder_2_out
  and and_6 (div, ~in_1[0], in_1[1], ~in_1[2], in_1[3], in_1[4], ~in_1[5]);  // AND_Gate
  and and_7 (divu, in_1[0], in_1[1], ~in_1[2], in_1[3], in_1[4], ~in_1[5]);  // AND_Gate
  and and_8 (slt, ~in_1[0], in_1[1], ~in_1[2], in_1[3], ~in_1[4], ~in_1[5]);  // AND_Gate
  and and_9 (sltu, ~in_1[0], in_1[1], ~in_1[2], in_1[3], in_1[4], ~in_1[5]);  // AND_Gate
  Multiplexer #(.width(32)) multiplexer_1 (.in0({32{1'b0}}), .in1(low_t), .out(low), .sel(in_2));  // open: en
  mult___mulu mult_mulu_1 (.in_1(in_3), .in_2(in_4), .in_3(con_signo), .hi(mult___mulu_hi), .lo(mult___mulu_lo));
  Multiplexer #(.width(32)) multiplexer_2 (.in0({32{1'b0}}), .in1(hi_t), .out(hi), .sel(in_2));  // open: en
  and and_10 (\and , ~in_1[0], ~in_1[1], in_1[2], ~in_1[3], ~in_1[4], in_1[5]);  // AND_Gate
  and and_11 (\or , in_1[0], ~in_1[1], in_1[2], ~in_1[3], ~in_1[4], in_1[5]);  // AND_Gate
  and and_12 (\nor , in_1[0], in_1[1], in_1[2], ~in_1[3], ~in_1[4], in_1[5]);  // AND_Gate
  and and_13 (\xor , ~in_1[0], ~in_1[1], ~in_1[2], in_1[3], ~in_1[4], in_1[5]);  // AND_Gate
  Multiplexer #(.select(4), .width(32)) multiplexer_3 (
    .in0(s_add), .in1(s_sub), .in2(mult___mulu_lo), .in3(mult___mulu_lo), .in4(div__divu_lo),
    .in5(div__divu_lo), .in6(slt___sltu), .in7(slt___sltu), .in8(s_and), .in9(s_or), .in10(s_nor),
    .in11(s_xor), .in12(s_xor), .out(low_t), .sel(priority_encoder_1_out));  // open: in13, in14, in15, en
  Multiplexer #(.select(4), .width(32)) multiplexer_4 (
    .in0({32{1'b0}}), .in1({32{1'b0}}), .in2(mult___mulu_hi), .in3(mult___mulu_hi), .in4(div__divu_hi),
    .in5(div__divu_hi), .in6({32{1'b0}}), .in7({32{1'b0}}), .in8({32{1'b0}}), .in9({32{1'b0}}),
    .in10({32{1'b0}}), .in11({32{1'b0}}), .in12({32{1'b0}}), .out(hi_t), .sel(priority_encoder_2_out));  // open: in13, in14, in15, en
  Comparator #(.width(32)) comparator_1 (.a(result), .b({32{1'b0}}), .eq(Output));  // open: gt, lt
  Comparator #(.width(32)) comparator_2 (.a(result), .b({32{1'b0}}), .lt(Output_2));  // open: gt, eq

  // Other names for the same wires on the sheet: Const[15:0] = in_5; EN = in_2; Func_Code[5:0] = in_1;
  //   Operacion[0] = con_signo; Rs[31:0] = in_3; Rt[31:0] = in_4

  // Notes on the sheet:
  //   add
  //   sub
  //   mul
  //   mulu
  //   Tipo R
  //   div
  //   divu
  //   slt
  //   sltu
  //   Calculos
  //   div divu
  //   and
  //   or
  //   nor
  //   xor
endmodule

module div___divu (
  input  [31:0] in_1,
  input  [31:0] in_2,
  input  in_3,
  output [31:0] Lo,
  output [31:0] Hi
);

  wire [31:0] div_a_negativo, div_b_negativo, div_negativos, div_positivos, divider_2_out, divider_3_out,
       Hi_sin_sg, Lo_sin_sg, minus_a, minus_b, resto_a_negativo, resto_b_negativo, resto_negativo,
       resto_positivo;

  Divider #(.width(32)) divider_1 (.a(in_1), .b(in_2), .out(div_positivos), .rem(resto_positivo));  // open: upper
  Divider #(.width(32)) divider_2 (.a(minus_a), .b(in_2), .out(divider_2_out), .rem(resto_a_negativo));  // open: upper
  Negator #(.width(32)) negator_1 (.in(divider_2_out), .out(div_a_negativo));
  Divider #(.width(32)) divider_3 (.a(in_1), .b(minus_b), .out(divider_3_out), .rem(resto_b_negativo));  // open: upper
  Negator #(.width(32)) negator_2 (.in(divider_3_out), .out(div_b_negativo));
  Divider #(.width(32)) divider_4 (.a(minus_a), .b(minus_b), .out(div_negativos), .rem(resto_negativo));  // open: upper
  // Probe on in_1
  Negator #(.width(32)) negator_3 (.in(in_1), .out(minus_a));
  // Probe on in_2
  Negator #(.width(32)) negator_4 (.in(in_2), .out(minus_b));
  // Probe on Lo
  Multiplexer #(.select(2), .width(32)) multiplexer_1 (
    .in0(div_positivos), .in1(div_a_negativo), .in2(div_b_negativo), .in3(div_negativos), .out(Lo_sin_sg),
    .sel({in_2[31], in_1[31]}));  // open: en
  Multiplexer #(.select(2), .width(32)) multiplexer_2 (
    .in0(resto_positivo), .in1(resto_a_negativo), .in2(resto_b_negativo), .in3(resto_negativo),
    .out(Hi_sin_sg), .sel({in_2[31], in_1[31]}));  // open: en
  // Probe on Hi
  Multiplexer #(.width(32), .enable("false")) multiplexer_3 (
    .in0(div_positivos), .in1(Lo_sin_sg), .out(Lo), .sel(in_3));
  Multiplexer #(.width(32), .enable("false")) multiplexer_4 (
    .in0(resto_positivo), .in1(Hi_sin_sg), .out(Hi), .sel(in_3));

  // Other names for the same wires on the sheet: a[31:0] = in_1; b[31:0] = in_2; con_sig = in_3; a_sig = in_1[31];
  //   selector[1:0] = {in_2[31], in_1[31]}; b_sg = in_2[31]

  // Notes on the sheet:
  //   0 : sin signo
  //   1 : con signo
endmodule

module mult___mulu (
  input  [31:0] in_1,
  input  [31:0] in_2,
  input  in_3,
  output [31:0] hi,
  output [31:0] lo
);

  wire [31:0] minus_a, minus_b, mult_hi, mult_lo, multiplexer_1_out, multiplexer_2_out, mulu_Hi, mulu_Lo,
       negator_1_out, negator_2_out;

  Multiplier #(.width(32)) multiplier_1 (.a(in_1), .b(in_2), .out(mult_lo), .cout(mult_hi));  // open: cin
  Negator #(.width(32)) negator_1 (.in(in_1), .out(negator_1_out));
  Negator #(.width(32)) negator_2 (.in(in_2), .out(negator_2_out));
  // Probe on in_1
  // Probe on multiplexer_1_out
  Multiplexer #(.width(32), .enable("false")) multiplexer_1 (
    .in0(in_1), .in1(negator_1_out), .out(multiplexer_1_out), .sel(in_1[31]));
  Multiplexer #(.width(32), .enable("false")) multiplexer_2 (
    .in0(in_2), .in1(negator_2_out), .out(multiplexer_2_out), .sel(in_2[31]));
  Negator #(.width(32)) negator_3 (.in(in_1), .out(minus_a));
  Multiplier #(.width(32)) multiplier_2 (
    .a(multiplexer_1_out), .b(multiplexer_2_out), .out(mulu_Lo), .cout(mulu_Hi));  // open: cin
  // Probe on multiplexer_2_out
  // Probe on in_2
  Negator #(.width(32)) negator_4 (.in(in_2), .out(minus_b));
  // Probe on lo
  // Probe on hi
  Multiplexer #(.width(32), .enable("false")) multiplexer_3 (.in0(mult_hi), .in1(mulu_Hi), .out(hi), .sel(in_3));
  Multiplexer #(.width(32), .enable("false")) multiplexer_4 (.in0(mult_lo), .in1(mulu_Lo), .out(lo), .sel(in_3));

  // Other names for the same wires on the sheet: a[31:0] = in_1; a_sig = in_1[31]; b[31:0] = in_2; b_sg = in_2[31];
  //   con_sig = in_3

  // Notes on the sheet:
  //   0 : sin signo
  //   1 : con signo
endmodule

module Multiplexer_6_bits_32 (
  input  [31:0] in_1,
  input  [31:0] in_2,
  input  [31:0] in_3,
  input  [31:0] in_4,
  input  [31:0] in_5,
  input  [31:0] in_6,
  input  [31:0] in_7,
  input  [31:0] in_8,
  input  [31:0] in_9,
  input  [31:0] in_10,
  input  [31:0] in_11,
  input  [31:0] in_12,
  input  [31:0] in_13,
  input  [31:0] in_14,
  input  [31:0] in_15,
  input  [31:0] in_16,
  input  [31:0] in_17,
  input  [31:0] in_18,
  input  [31:0] in_19,
  input  [31:0] in_20,
  input  [31:0] in_21,
  input  [31:0] in_22,
  input  [31:0] in_23,
  input  [31:0] in_24,
  input  [31:0] in_25,
  input  [31:0] in_26,
  input  [31:0] in_27,
  input  [31:0] in_28,
  input  [31:0] in_29,
  input  [31:0] in_30,
  input  [31:0] in_31,
  input  [31:0] in_32,
  input  [31:0] in_33,
  input  [31:0] in_34,
  input  [31:0] in_35,
  input  [31:0] in_36,
  input  [31:0] in_37,
  input  [31:0] in_38,
  input  [31:0] in_39,
  input  [31:0] in_40,
  input  [31:0] in_41,
  input  [31:0] in_42,
  input  [31:0] in_43,
  input  [31:0] in_44,
  input  [31:0] in_45,
  input  [31:0] in_46,
  input  [31:0] in_47,
  input  [31:0] in_48,
  input  [31:0] in_49,
  input  [31:0] in_50,
  input  [31:0] in_51,
  input  [31:0] in_52,
  input  [31:0] in_53,
  input  [31:0] in_54,
  input  [31:0] in_55,
  input  [31:0] in_56,
  input  [31:0] in_57,
  input  [31:0] in_58,
  input  [31:0] in_59,
  input  [31:0] in_60,
  input  [31:0] in_61,
  input  [31:0] in_62,
  input  [31:0] in_63,
  input  [31:0] in_64,
  output [31:0] S
);

  wire [31:0] S1, S2;

  Multiplexer #(.select(5), .width(32)) multiplexer_1 (
    .in0(in_1), .in1(in_2), .in2(in_3), .in3(in_4), .in4(in_5), .in5(in_6), .in6(in_7), .in7(in_8),
    .in8(in_9), .in9(in_10), .in10(in_11), .in11(in_12), .in12(in_13), .in13(in_14), .in14(in_15),
    .in15(in_16), .in16(in_17), .in17(in_18), .in18(in_19), .in19(in_20), .in20(in_21), .in21(in_22),
    .in22(in_23), .in23(in_24), .in24(in_25), .in25(in_26), .in26(in_27), .in27(in_28), .in28(in_29),
    .in29(in_30), .in30(in_31), .in31(in_32), .out(S1));  // open: sel, en
  Multiplexer #(.select(5), .width(32)) multiplexer_2 (
    .in0(in_33), .in1(in_35), .in2(in_35), .in3(in_36), .in4(in_37), .in5(in_38), .in6(in_39), .in7(in_40),
    .in8(in_41), .in9(in_42), .in10(in_43), .in11(in_44), .in12(in_45), .in13(in_46), .in14(in_47),
    .in15(in_48), .in16(in_49), .in17(in_50), .in18(in_51), .in19(in_52), .in20(in_53), .in21(in_54),
    .in22(in_55), .in23(in_56), .in24(in_57), .in25(in_58), .in26(in_59), .in27(in_60), .in28(in_61),
    .in29(in_62), .in30(in_63), .in31(in_64), .out(S2));  // open: sel, en
  Multiplexer #(.select(2), .width(32)) multiplexer_3 (.in0(S1), .in3(S2), .out(S));  // open: in1, in2, sel, en

  // Other names for the same wires on the sheet: _1[31:0] = in_1; _2[31:0] = in_2; _3[31:0] = in_3; _4[31:0] = in_4;
  //   _5[31:0] = in_5; _6[31:0] = in_6; _7[31:0] = in_7; _8[31:0] = in_8; _9[31:0] = in_9; _10[31:0] = in_10;
  //   _11[31:0] = in_11; _12[31:0] = in_12; _13[31:0] = in_13; _14[31:0] = in_14; _15[31:0] = in_15;
  //   _16[31:0] = in_16; _17[31:0] = in_17; _18[31:0] = in_18; _19[31:0] = in_19; _20[31:0] = in_20;
  //   _21[31:0] = in_21; _22[31:0] = in_22; _23[31:0] = in_23; _24[31:0] = in_24; _25[31:0] = in_25;
  //   _26[31:0] = in_26; _27[31:0] = in_27; _28[31:0] = in_28; _29[31:0] = in_29; _30[31:0] = in_30;
  //   _31[31:0] = in_31; _32[31:0] = in_32; _33[31:0] = in_33; _34[31:0] = in_34; _35[31:0] = in_35;
  //   _36[31:0] = in_36; _37[31:0] = in_37; _38[31:0] = in_38; _39[31:0] = in_39; _40[31:0] = in_40;
  //   _41[31:0] = in_41; _42[31:0] = in_42; _43[31:0] = in_43; _44[31:0] = in_44; _45[31:0] = in_45;
  //   _46[31:0] = in_46; _47[31:0] = in_47; _48[31:0] = in_48; _49[31:0] = in_49; _50[31:0] = in_50;
  //   _51[31:0] = in_51; _52[31:0] = in_52; _53[31:0] = in_53; _54[31:0] = in_54; _55[31:0] = in_55;
  //   _56[31:0] = in_56; _57[31:0] = in_57; _58[31:0] = in_58; _59[31:0] = in_59; _60[31:0] = in_60;
  //   _61[31:0] = in_61; _62[31:0] = in_62; _63[31:0] = in_63; _64[31:0] = in_64
endmodule

module Data_Path (
  input  in_1,
  input  in_2,
  input  [31:0] in_3,
  input  in_4,
  input  in_5,
  output _0,
  output negativo
);

  wire EN_PC, SF, tipo_I, tipo_J, tipo_P, tipo_R, ZF;
  wire [4:0] instruction_decoder_1_rd, instruction_decoder_1_rs, instruction_decoder_1_rt;
  wire [5:0] Func_Code, Op_Code;
  wire [15:0] Const;
  wire [31:0] A, alu_r_1_low, B, multiplexer_1_out, multiplexer_2_out, out_I, register_1_q;

  Multiplexer #(.width(32), .enable("false")) multiplexer_1 (.in1(out_I), .out(multiplexer_1_out));  // open: in0, sel
  Register #(.width(32)) register_1 (.D(multiplexer_1_out), .en(EN_PC), .Q(register_1_q), .clk(in_1));  // open: clr
  or or_1 (EN_PC, tipo_I, in_5, tipo_J);
  // ALU_I alu_i_1: pin names not known; wires that end beside it: Op_Code, A, B, tipo_I, out_I
  Instruction_Decoder instruction_decoder_1 (
    .in_1(register_1_q), .Op_Code(Op_Code), .Rt(instruction_decoder_1_rt), .Constante(Const),
    .Func_Code(Func_Code), .Rd(instruction_decoder_1_rd), .Rs(instruction_decoder_1_rs), .Output(tipo_R),
    .Output_2(tipo_I), .Output_3(tipo_P), .Output_4(tipo_J));  // open: x, Destino_salto
  Multiplexer #(.select(2), .width(32)) multiplexer_2 (
    .in0(alu_r_1_low), .in1(A), .in3(in_3), .out(multiplexer_2_out));  // open: in2, sel, en
  Register_File register_file_1 (
    .in_1(multiplexer_2_out), .in_2(in_4), .in_4(instruction_decoder_1_rd), .in_3(instruction_decoder_1_rs),
    .in_6(in_2), .in_5(instruction_decoder_1_rt), .in_7(in_1), .Sa(A), .Sb(B));  // open: in_8
  ALU_R alu_r_1 (
    .in_1(Func_Code), .in_3(A), .in_4(B), .in_5(Const), .in_2(tipo_R), .low(alu_r_1_low), .Output(ZF),
    .Output_2(SF));  // open: hi

  // Other names for the same wires on the sheet: CU_EN_PC = in_5; leer_escribir = in_4; Ram_out[31:0] = in_3;
  //   reloj = in_1; reset = in_2

  // Notes on the sheet:
  //   PC
endmodule

module Branch_Counter (
  input  in_1,
  input  in_2,
  input  [25:0] in_3,
  output [25:0] Output
);


  // Other names for the same wires on the sheet: destino_salto[25:0] = in_3; salto = in_1; salto_regular = in_2
endmodule

module selector_func (
  input  [5:0] in_1,
  input  [1:0] in_2
);


  // Other names for the same wires on the sheet: Func_Code[5:0] = in_1; tipo_instruccion[1:0] = in_2
endmodule

module ALU_I (
  input  [5:0] in_1,
  input  in_2,
  input  [15:0] in_3,
  input  [31:0] in_4,
  input  [31:0] in_5,
  output [31:0] Output
);

  wire addi, andi, beq, bgtz, blez, bltz, bne, lw, slti, sltiu, sw;
  wire [3:0] priority_encoder_1_out;
  wire [31:0] out, r_addi, r_andi_ori_xori, r_slti_ltiu, r_sltisltiu, s_beq, s_bgtz, s_blez, s_bltz, s_bne,
       s_lw, s_sw;

  addi addi_1 (.Rs(in_4), .cons(in_3), .Output(r_addi));
  slti___sltiu slti_sltiu_1 (.in_1(in_1[0]), .Rs(in_4), .\const (in_3), .Output(r_sltisltiu));
  and and_1 (beq, ~in_1[0], ~in_1[1], in_1[2], ~in_1[3], ~in_1[4], ~in_1[5]);  // AND_Gate
  and and_2 (bne, in_1[0], ~in_1[1], in_1[2], ~in_1[3], ~in_1[4], ~in_1[5]);  // AND_Gate
  andi___ori__xori andi_ori_xori_1 (.Rs(in_4), .cons(in_3), .Output(r_andi_ori_xori));
  Priority_Encoder #(.select(4)) priority_encoder_1 (
    .in0(beq), .in1(bne), .in2(blez), .in3(bgtz), .in4(bltz), .in5(addi), .in6(slti), .in7(sltiu), .in8(lw),
    .in9(sw), .in10(andi), .out(priority_encoder_1_out));  // open: in11, in12, in13, in14, in15, gs, en_out, en_in
  // Probe on priority_encoder_1_out
  and and_3 (blez, ~in_1[0], in_1[1], in_1[2], ~in_1[3], ~in_1[4], ~in_1[5]);  // AND_Gate
  and and_4 (bgtz, in_1[0], in_1[1], in_1[2], ~in_1[3], ~in_1[4], ~in_1[5]);  // AND_Gate
  Multiplexer #(.width(32)) multiplexer_1 (.in0({32{1'b0}}), .in1(out), .out(Output), .sel(in_2));  // open: en
  and and_5 (bltz, in_1[0], ~in_1[1], ~in_1[2], ~in_1[3], ~in_1[4], ~in_1[5]);  // AND_Gate
  and and_6 (addi, ~in_1[0], ~in_1[1], ~in_1[2], in_1[3], ~in_1[4], ~in_1[5]);  // AND_Gate
  Multiplexer #(.select(4), .width(32)) multiplexer_2 (
    .in0(s_beq), .in1(s_bne), .in2(s_blez), .in3(s_bgtz), .in4(s_bltz), .in5(r_addi), .in6(r_slti_ltiu),
    .in7(r_slti_ltiu), .in8(s_lw), .in9(s_sw), .in10(r_andi_ori_xori), .out(out), .sel(priority_encoder_1_out));  // open: in11, in12, in13, in14, in15, en
  and and_7 (slti, ~in_1[0], in_1[1], ~in_1[2], in_1[3], ~in_1[4], ~in_1[5]);  // AND_Gate
  and and_8 (sltiu, in_1[0], in_1[1], ~in_1[2], in_1[3], ~in_1[4], ~in_1[5]);  // AND_Gate
  and and_9 (lw, in_1[0], in_1[1], ~in_1[2], ~in_1[3], ~in_1[4], in_1[5]);  // AND_Gate
  and and_10 (sw, in_1[0], in_1[1], ~in_1[2], in_1[3], ~in_1[4], in_1[5]);  // AND_Gate
  and and_11 (andi, ~in_1[0], ~in_1[1], in_1[2], in_1[3], ~in_1[4], ~in_1[5]);  // AND_Gate

  // Other names for the same wires on the sheet: Const[15:0] = in_3; EN = in_2; con_signo = in_1[0];
  //   Func_Code[5:0] = in_1; Rs[31:0] = in_4; Rt[31:0] = in_5

  // Notes on the sheet:
  //   beq
  //   bne
  //   blez
  //   bgtz
  //   Tipi I
  //   bltz
  //   addi
  //   slti
  //   sltiu
  //   lw
  //   sw
  //   andi
endmodule
